# Fritzing sketch clock_half (saved by Fritzing 1.0.2b)
breadboards: 1

parts:
  ZS-042_RTC1 = ZS-042 RTC Module  # not connected
  S1 = Pushbutton [package="[THT]"]
  Grove1 = TM1637 7segment 4digit display
  Grove2 = TM1637 7segment 4digit display
  Grove3 = TM1637 7segment 4digit display
  WeMos_D1_Mini1 = WeMos D1 Mini  # not connected
  X2 = USB Connectors [package=usb-microb]  # not connected

nets:
  N1: S1.Pin_1, S1.Pin_2
  N2: S1.Pin_3, S1.Pin_4
  VCC: Grove1.Vcc, Grove2.Vcc, Grove3.Vcc
  GND: Grove1.GND, Grove2.GND, Grove3.GND
  N3: Grove1.CLK, Grove2.CLK, Grove3.CLK

notes:
  rtc3231
  D1 - SCL
  D2 - SDA
  D7 - SQW
  tm1637
  D3 - CLK
  D4 - SDA yyyy
  D5 - SDA hhmm
  D6 - SDA ssuu
  hhmm
  yyyy
  ssuu
